# Fritzing sketch posenet_BT_tracking (saved by Fritzing 0.9.3b)
breadboards: 1

parts:
  元件1 = Arduino Nano (Rev3.0) (ICSP)
  元件2 = Bluetooth Mate Silver
  nano_5V = Power plug
  FIRE_Servo = Basic Servo
  Y-Servo = Basic Servo
  X-Servo = Basic Servo
  Servo_power = Power plug [part_number="Servo 5V"]

nets:
  GND: 元件1.GND, 元件2.GND, nano_5V.GND, FIRE_Servo.gnd, Y-Servo.gnd, X-Servo.gnd, Servo_power.GND
  N1: 元件1.D2, 元件2.TX_5V
  N2: 元件1.D4, 元件2.RX_5V
  N3: 元件1.D9, X-Servo.pulse
  N4: 元件1.D10, Y-Servo.pulse
  N5: 元件1.D11/MOSI, FIRE_Servo.pulse
  VCC: 元件1.5V, 元件2.VCC, nano_5V.VCC
  VCC_2: X-Servo.vcc, Servo_power.VCC
